// Logisim project PROJETO - CD.circ as structural Verilog: 5 circuits, main circuit main
module main (
  input  in_1,
  input  in_2,
  input  in_3,
  input  in_4,
  input  JOGADOR_0,
  input  in_6,
  input  in_7,
  input  in_8,
  input  JOGADOR
);

  wire JOGAR_out, jogo_1_out_5, jogo_1_out_6, jogo_1_out_7;
  wire [3:0] decodificador_1_inferior, decodificador_1_superior, decodificador_2_inferior,
       decodificador_2_superior;

  _7_Segment_Display u_7_segment_display_1 (
    .g(decodificador_1_superior[3]), .f(decodificador_1_superior[2]), .a(decodificador_1_superior[1]),
    .b(decodificador_1_superior[0]), .e(decodificador_1_inferior[3]), .d(decodificador_1_inferior[2]),
    .c(decodificador_1_inferior[1]), .dp(decodificador_1_inferior[0]));
  DECODIFICADOR decodificador_1 (
    .in_1({in_1, in_2, in_3, in_4}), .SUPERIOR(decodificador_1_superior), .INFERIOR(decodificador_1_inferior));
  _7_Segment_Display u_7_segment_display_2 (
    .g(decodificador_2_superior[3]), .f(decodificador_2_superior[2]), .a(decodificador_2_superior[1]),
    .b(decodificador_2_superior[0]), .e(decodificador_2_inferior[3]), .d(decodificador_2_inferior[2]),
    .c(decodificador_2_inferior[1]), .dp(decodificador_2_inferior[0]));
  DECODIFICADOR decodificador_2 (
    .in_1({JOGADOR_0, in_6, in_7, in_8}), .SUPERIOR(decodificador_2_superior),
    .INFERIOR(decodificador_2_inferior));
  Button JOGAR (.out(JOGAR_out));
  JOGO jogo_1 (
    .in_2({in_1, in_2, in_3, in_4}), .in_3({JOGADOR_0, in_6, in_7, in_8}), .JOGAR(JOGAR_out),
    .JOGADOR(JOGADOR), .out_5(jogo_1_out_5), .out_6(jogo_1_out_6), .out_7(jogo_1_out_7));
  LED MENOR (.in(jogo_1_out_5));
  LED ACERTOU (.in(jogo_1_out_6));
  LED MAIOR (.in(jogo_1_out_7));

  // Notes on the sheet:
  //   JOGADOR 1
endmodule

// DEC
module DECODIFICADOR (
  input  [3:0] in_1,
  output [3:0] SUPERIOR,
  output [3:0] INFERIOR
);

  wire and_1_out, and_2_out, and_3_out, and_4_out, and_5_out, and_6_out, and_7_out, and_8_out, and_9_out,
       and_10_out, and_11_out, and_12_out, and_13_out, and_14_out, and_15_out, and_16_out, and_17_out,
       and_18_out, and_19_out, and_20_out, and_21_out, and_22_out, and_23_out, nand_1_out, nor_1_out,
       nor_2_out, nor_3_out, nor_4_out, nor_5_out, or_1_out, or_2_out, or_3_out, or_4_out, or_5_out,
       or_6_out, or_7_out, or_8_out, xor_1_out, xor_2_out, xor_3_out;

  nor nor_1 (nor_1_out, in_1[3], in_1[2]);
  xor xor_1 (xor_1_out, in_1[2], in_1[0]);
  or or_1 (or_1_out, ~in_1[2], in_1[1]);  // OR_Gate
  or or_2 (or_2_out, in_1[2], in_1[1]);
  and and_1 (and_1_out, in_1[3], in_1[1]);
  and and_2 (and_2_out, in_1[3], ~in_1[2]);  // AND_Gate
  nor nor_2 (nor_2_out, in_1[1], in_1[0]);
  and and_3 (and_3_out, in_1[2], ~in_1[0]);  // AND_Gate
  and and_4 (and_4_out, ~in_1[1], in_1[2], ~in_1[3]);  // AND_Gate
  and and_5 (and_5_out, in_1[1], ~in_1[0]);  // AND_Gate
  and and_6 (and_6_out, in_1[3], ~in_1[2]);  // AND_Gate
  and and_7 (and_7_out, in_1[3], in_1[0]);
  and and_8 (and_8_out, ~in_1[3], in_1[2], ~in_1[1]);  // AND_Gate
  and and_9 (and_9_out, ~in_1[2], in_1[1], in_1[0]);  // AND_Gate
  or or_3 (or_3_out, in_1[2], in_1[1]);
  or or_4 (or_4_out, in_1[3], ~in_1[2]);  // OR_Gate
  or or_5 (or_5_out, ~in_1[3], in_1[2]);  // OR_Gate
  and and_10 (and_10_out, ~in_1[3], in_1[2], in_1[0]);  // AND_Gate
  and and_11 (and_11_out, in_1[3], ~in_1[2], ~in_1[1]);  // AND_Gate
  xor xor_2 (xor_2_out, in_1[3], in_1[1]);
  nand nand_1 (nand_1_out, in_1[3], in_1[0]);
  xor xor_3 (xor_3_out, in_1[3], in_1[2]);
  and and_12 (and_12_out, in_1[1], in_1[0]);
  nor nor_3 (nor_3_out, in_1[1], in_1[0]);
  and and_13 (and_13_out, in_1[2], in_1[0]);
  nor nor_4 (nor_4_out, in_1[2], in_1[0]);
  or or_6 (or_6_out, nor_1_out, xor_1_out);
  and and_14 (and_14_out, ~in_1[0], or_1_out);  // AND_Gate
  and and_15 (and_15_out, or_2_out, in_1[3]);
  and and_16 (and_16_out, or_4_out, ~in_1[0]);  // AND_Gate
  and and_17 (and_17_out, in_1[1], or_5_out);
  and and_18 (and_18_out, xor_2_out, in_1[0]);
  and and_19 (and_19_out, nand_1_out, ~in_1[2]);  // AND_Gate
  nor nor_5 (nor_5_out, in_1[3], in_1[1], in_1[0]);
  and and_20 (and_20_out, ~in_1[1], in_1[0]);  // AND_Gate
  or or_7 (or_7_out, and_12_out, nor_3_out);
  or or_8 (or_8_out, and_13_out, in_1[3], nor_4_out);
  and and_21 (and_21_out, or_8_out, ~in_1[1]);  // AND_Gate
  and and_22 (and_22_out, in_1[1], or_6_out);
  and and_23 (and_23_out, or_7_out, ~in_1[3]);  // AND_Gate
  or A (SUPERIOR[1], and_16_out, and_17_out, and_10_out, and_11_out);
  or B (SUPERIOR[0], and_18_out, and_19_out, nor_5_out);
  or C (INFERIOR[1], xor_3_out, and_20_out, and_23_out);
  or D (INFERIOR[2], and_21_out, and_22_out);
  or E (INFERIOR[3], and_14_out, and_15_out);
  or F (SUPERIOR[2], and_1_out, and_2_out, nor_2_out, and_3_out, and_4_out);
  or G (SUPERIOR[3], and_5_out, and_6_out, and_7_out, and_8_out, and_9_out);
  and and_24 (INFERIOR[0], in_1[3], or_3_out);

  // Notes on the sheet:
  //   W
  //   X
  //   Y
  //   Z
  //   ======================================================================
  //   ======================================================================
  //   ======================================================================
  //   ======================================================================
  //   ======================================================================
  //   ======================================================================
  //   ======================================================================
endmodule

// CMP
module COMPARADOR (
  input  [3:0] CHUTE,
  output [2:0] out_2
);

  wire _0_2_out, _0_out, _1_2_out, _1_out, _2_2_out, _2_out, _3_2_out, _3_out;

  xnor _0 (_0_out, 1'b1, CHUTE[0]);
  xnor _1 (_1_out, 1'b1, CHUTE[1]);
  xnor _2 (_2_out, 1'b1, CHUTE[2]);
  xnor _3 (_3_out, 1'b0, CHUTE[3]);
  and _0_2 (_0_2_out, CHUTE[0], _1_out, _2_out, _3_out, ~1'b1);  // AND_Gate
  and _1_2 (_1_2_out, CHUTE[1], ~1'b1, _2_out, _3_out);  // AND_Gate
  and _2_2 (_2_2_out, CHUTE[2], ~1'b1, _3_out);  // AND_Gate
  and _3_2 (_3_2_out, CHUTE[3], ~1'b0);  // AND_Gate
  and IGUAL (out_2[1], _0_out, _1_out, _2_out, _3_out);
  or MAIOR (out_2[2], _0_2_out, _1_2_out, _2_2_out, _3_2_out);
  nor MENOR (out_2[0], out_2[1], out_2[2]);

  // Notes on the sheet:
  //   N. MAGIC
endmodule

module JOGO (
  input  JOGAR,
  input  [3:0] in_2,
  input  [3:0] in_3,
  input  JOGADOR,
  output out_5,
  output out_6,
  output out_7
);

  wire [2:0] comparador_1_out_2;
  wire [3:0] multplexador_1_out_4;

  MULTPLEXADOR multplexador_1 (.in_1(in_2), .in_2(in_3), .in_3(JOGADOR), .out_4(multplexador_1_out_4));
  COMPARADOR comparador_1 (.CHUTE(multplexador_1_out_4), .out_2(comparador_1_out_2));
  and MENOR (out_5, JOGAR, comparador_1_out_2[0]);
  and IGUAL (out_6, JOGAR, comparador_1_out_2[1]);
  and MAIOR (out_7, JOGAR, comparador_1_out_2[2]);
endmodule

// MLT
module MULTPLEXADOR (
  input  [3:0] in_1,
  input  [3:0] in_2,
  input  in_3,
  output [3:0] out_4
);

  wire [3:0] and_4_out, and_5_out;

  and and_1 (and_4_out[3], in_1[3], in_3);
  and and_2 (and_4_out[2], in_1[2], in_3);
  and and_3 (and_4_out[1], in_1[1], in_3);
  and and_4 (and_4_out[0], in_1[0], in_3);
  and and_5 (and_5_out[0], ~in_3, in_2[0]);  // AND_Gate
  and and_6 (and_5_out[1], ~in_3, in_2[1]);  // AND_Gate
  and and_7 (and_5_out[2], ~in_3, in_2[2]);  // AND_Gate
  and and_8 (and_5_out[3], ~in_3, in_2[3]);  // AND_Gate
  assign out_4 = and_4_out | and_5_out;  // OR_Gate or_1, 4 bits wide
endmodule
